# Fritzing sketch Sketch_Physiradio (saved by Fritzing 0.8.7b)

parts:
  VS1053 = Arduino MP3 Player Shield
  WeMos_D1_Mini = WeMos D1 Mini
  SP1 = SPEAKER [package=pcb_mount_speaker]
  Componente1 = Adafruit VS1053 Codec + MicroSD Breakout - MP3/WAV/MIDI/OGG [part_number="Adafruit #1381"]  # not connected
  LED_STRIP_RGB_4-PIN = WS2801 [package=sop-14]

nets:
  N1: VS1053.RIGHT, SP1.-
  N2: VS1053.LEFT, SP1.+
  VCC: VS1053.VCC, WeMos_D1_Mini.5V, LED_STRIP_RGB_4-PIN.VCC
  N3: VS1053.MP3-DREQ, WeMos_D1_Mini.D2
  N4: VS1053.5V-MP3-CS, WeMos_D1_Mini.D1
  N5: VS1053.5V-MP3-DCS, WeMos_D1_Mini.D0
  N6: VS1053.5V-MOSI, WeMos_D1_Mini.D7
  N7: VS1053.MISO, WeMos_D1_Mini.D6
  N8: VS1053.5V-SCK, WeMos_D1_Mini.D5
  GND: VS1053.GND, WeMos_D1_Mini.G, LED_STRIP_RGB_4-PIN.GND
  N9: WeMos_D1_Mini.D3, LED_STRIP_RGB_4-PIN.SDI
  N10: WeMos_D1_Mini.D4, LED_STRIP_RGB_4-PIN.CKI

notes:
  Right and Left are welded in a 3.5 strereo jack, which can produce sound thanks to VS1053 3W amplifier
  This mp3 shield is not the same used in the real device. The exact VS1053 doesn't exist for Fritzing and this one is similar

custom parts:
  Adafruit VS1053 Codec + MicroSD Breakout - MP3/WAV/MIDI/OGG: This breakout board is the ultimate companion for the VLSI VS1053B DSP codec chip. The VS1053 can decode a wide variety of audio formats such as MP3, AAC, Ogg Vorbis, WMA, MIDI, FLAC, WAV (PCM and ADPCM). It can also be used to record audio in both PCM (WAV) and compressed Ogg Vorbis. You can do all sorts of stuff with the audio as well such as adjusting bass, treble, and volume digitally.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
