# Fritzing sketch Sketch_PhysiradioNEW (saved by Fritzing 0.8.7b)
circuit board: 10.9693cm x 9.7708cm

parts:
  WeMos_D1_Mini = WeMos D1 Mini
  Speaker_(4ohm) = SPEAKER [package=pcb_mount_speaker]
  WS2801_Led_Strip = LPD8806 RGB LED Strip
  VS1003/1053_MP3_Codec_(LC_Technology) = Adafruit VS1053 Codec + MicroSD Breakout - MP3/WAV/MIDI/OGG [part_number="Adafruit #1381"]

nets:
  3V3: WeMos_D1_Mini.3V3, WS2801_Led_Strip.+5V
  5V: WeMos_D1_Mini.5V, VS1003/1053_MP3_Codec_(LC_Technology).VIN
  N1: WeMos_D1_Mini.D0, VS1003/1053_MP3_Codec_(LC_Technology).XDCS_5V
  N2: WeMos_D1_Mini.D1, VS1003/1053_MP3_Codec_(LC_Technology).CS_5V
  N3: WeMos_D1_Mini.D2, VS1003/1053_MP3_Codec_(LC_Technology).DREQ
  N4: WeMos_D1_Mini.D3, WS2801_Led_Strip.DI
  N5: WeMos_D1_Mini.D4, WS2801_Led_Strip.CI
  N6: WeMos_D1_Mini.D5, VS1003/1053_MP3_Codec_(LC_Technology).SCLK_5V
  N7: WeMos_D1_Mini.D6, VS1003/1053_MP3_Codec_(LC_Technology).MISO
  N8: WeMos_D1_Mini.D7, VS1003/1053_MP3_Codec_(LC_Technology).MOSI_5V
  GND: WeMos_D1_Mini.G, WS2801_Led_Strip.GND, VS1003/1053_MP3_Codec_(LC_Technology).GND
  N9: Speaker_(4ohm).+, VS1003/1053_MP3_Codec_(LC_Technology).L_OUT
  N10: Speaker_(4ohm).-, VS1003/1053_MP3_Codec_(LC_Technology).R_OUT

notes:
  Right and Left are welded in a 3.5 strereo jack, which can produce sound thanks to VS1053 3W amplifier
  This mp3 shield is not the same used in the real device. The exact VS1053 doesn't exist for Fritzing and this one is similar
  Right and Left are welded in a 3.5 strereo jack, which can produce sound thanks to VS1053 3W amplifier
  la componente attualmente in uso é una striscia led WS2801, dove CI é CLK (clock) e DI é SD

custom parts:
  LPD8806 RGB LED Strip: Digitally addressable RGB LED strip
  Adafruit VS1053 Codec + MicroSD Breakout - MP3/WAV/MIDI/OGG: This breakout board is the ultimate companion for the VLSI VS1053B DSP codec chip. The VS1053 can decode a wide variety of audio formats such as MP3, AAC, Ogg Vorbis, WMA, MIDI, FLAC, WAV (PCM and ADPCM). It can also be used to record audio in both PCM (WAV) and compressed Ogg Vorbis. You can do all sorts of stuff with the audio as well such as adjusting bass, treble, and volume digitally.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
